# Fritzing sketch Discoball (saved by Fritzing 0.9.3b)
circuit board: 10.8913cm x 5.26082cm
breadboards: 1

parts:
  D1 = Diode [package=diode-1n4148]
  Q1 = TRANSISTOR_NPN [package=to-92-ammo]
  U1 = RELAY [package=relay-jzc]
  J1 = Camdenboss CTB0158-3 [part_number=CTB0158-3 package=THT]
  J2 = Camdenboss CTB0158-2 [part_number=CTB0158-2 package=THT]
  U2 = RELAY [package=relay-jzc]
  D2 = Diode [package=diode-1n4148]
  Q2 = TRANSISTOR_NPN [package=to-92-ammo]
  J4 = Camdenboss CTB0158-2 [part_number=CTB0158-2 package=THT]
  U3 = RELAY [package=relay-jzc]
  D3 = Diode [package=diode-1n4148]
  Q3 = TRANSISTOR_NPN [package=to-92-ammo]
  J6 = Camdenboss CTB0158-2 [part_number=CTB0158-2 package=THT]
  U4 = RELAY [package=relay-jzc]
  D4 = Diode [package=diode-1n4148]
  Q4 = TRANSISTOR_NPN [package=to-92-ammo]
  J8 = Camdenboss CTB0158-2 [part_number=CTB0158-2 package=THT]
  J3 = Camdenboss CTB0158-2 [part_number=CTB0158-2 package=THT]
  J5 = Camdenboss CTB0158-2 [part_number=CTB0158-2 package=THT]
  J7 = Camdenboss CTB0158-2 [part_number=CTB0158-2 package=THT]
  R3 = Resistor [tolerance=±5% resistance=1k package=THT]
  R5 = Resistor [tolerance=±5% resistance=1k package=THT]
  R7 = Resistor [tolerance=±5% resistance=1k package=THT]
  R4 = Resistor [tolerance=±5% resistance=10k package=THT]
  R6 = Resistor [tolerance=±5% resistance=10k package=THT]
  R8 = Resistor [tolerance=±5% resistance=10k package=THT]
  R1 = Resistor [tolerance=±5% resistance=1k package=THT]
  R2 = Resistor [tolerance=±5% resistance=10k package=THT]

nets:
  N1: D1.A, Q1.C, U1.COIL2
  N2: D1.C, Q1.E, U1.COIL1, J1.pin1, J1.pin3, U2.COIL1, D2.C, Q2.E, U3.COIL1, D3.C, Q3.E, U4.COIL1, D4.C, Q4.E, J3.pin1, J5.pin1, J7.pin1, R4.Pin_1, R6.Pin_1, R8.Pin_1, R2.Pin_1
  N3: Q1.B, R1.Pin_1
  N4: U1.NO, J2.pin1
  N5: U1.MAIN, J2.pin2
  N6: J1.pin2, R1.Pin_0, R2.Pin_0
  N7: U2.COIL2, D2.A, Q2.C
  N8: U2.NO, J4.pin1
  N9: U2.MAIN, J4.pin2
  N10: Q2.B, R3.Pin_1
  N11: U3.COIL2, D3.A, Q3.C
  N12: U3.NO, J6.pin1
  N13: U3.MAIN, J6.pin2
  N14: Q3.B, R5.Pin_1
  N15: U4.COIL2, D4.A, Q4.C
  N16: U4.NO, J8.pin1
  N17: U4.MAIN, J8.pin2
  N18: Q4.B, R7.Pin_1
  N19: J3.pin2, R3.Pin_0, R4.Pin_0
  N20: J5.pin2, R5.Pin_0, R6.Pin_0
  N21: J7.pin2, R7.Pin_0, R8.Pin_0

notes:
  -
  +
