# Fritzing sketch ESP8266-power (saved by Fritzing 0.9.3b)
circuit board: 8.80418cm x 4.80066cm
breadboards: 1

parts:
  IC1 = V_REG_LD1117VXX [package=78xxl]
  Power_In_5V = Power plug
  C1 = Electrolytic Capacitor [capacitance=10µF package="200 mil [THT, electrolytic]"]
  C2 = Electrolytic Capacitor [capacitance=10µF package="200 mil [THT, electrolytic]"]
  Power_Out_3_3V = Power plug

nets:
  N1: IC1.OUT, C2.+, Power_Out_3_3V.VCC
  GND: IC1.GND, Power_In_5V.GND, C1.-, C2.-, Power_Out_3_3V.GND
  N2: IC1.IN, Power_In_5V.VCC, C1.+
