# Fritzing sketch ESP8266-shiftregister (saved by Fritzing 0.9.3b)
circuit board: 8.46667cm x 5.64444cm
breadboards: 1

parts:
  U1 = ESP8266 WiFi Module [part_number=ESP8266]
  U2 = 74HC595 [package="DIP16 [THT]"]
  J1 = Camdenboss CTB0158-4 [part_number=CTB0158-4 package=THT]
  Raspberry_Pi_1 = Raspberry Pi 3 [part_number=RPI-3-V1.2]
  R1 = Resistor [tolerance=±5% resistance=10k package="2512 [SMD]"]

nets:
  N1: U1.RXD, Raspberry_Pi_1.GIPO14
  VCC: U1.VCC, U2.MR, U2.VCC, Raspberry_Pi_1.3v3, R1.Pin_0
  N2: U1.GPIO_0, U2.DS
  N3: U1.GPIO_2, U2.SH_CP
  N4: U1.CH_PD, R1.Pin_1
  GND: U1.GND, U2.OE, Raspberry_Pi_1.GND
  N5: U1.TXD, U2.ST_CP
  N6: U2.Q1, J1.pin3
  N7: U2.Q2, J1.pin2
  N8: U2.Q3, J1.pin1
  N9: U2.Q0, J1.pin4

custom parts:
  ESP8266 WiFi Module: Generic WiFi Module based on the ESP8266 with onboard PCB antenna and UART communications
